# Fritzing sketch Invernadero_SIGNOS_Circuito (saved by Fritzing 0.9.2b)
breadboards: 2

parts:
  Parte1 = Arduino Uno (Rev3)
  R1 = Photocell (LDR) [package=THT]
  R2 = Resistor [tolerance=±5% resistance=10k package=THT]
  T1 = LM35 Temperature Sensor [package="TO92 [THT]"]
  U1 = LCD-16X2 [package=lcd-16x2_noholes]
  LED1 = smd LED [color="Red (633nm)" package="0805 [SMD]"]
  LED2 = smd LED [color="Red (633nm)" package="0805 [SMD]"]
  R3 = Resistor [tolerance=±10% resistance=1k package=THT]
  R4 = Resistor [tolerance=±10% resistance=1k package=THT]
  M1 = DC Motor
  D1 = Rectifier Diode [part_number=1N4001 package="300 mil [THT]"]
  S1 = Pushbutton [package="[THT]"]
  R5 = Resistor [tolerance=±5% resistance=1k package=THT]

nets:
  N1: Parte1.A0, R1.pin_1, R2.Pin_0
  N2: Parte1.A1, T1.Vout
  N3: Parte1.D9_PWM, R4.Pin_1
  N4: Parte1.D10_PWM/SS, D1.anode
  N5: Parte1.D11_PWM/MOSI, U1.R_W
  N6: Parte1.D12/MISO, U1.RS
  GND: Parte1.GND, R2.Pin_1, T1.GND, U1.VSS, U1.K, LED1.cathode, LED2.cathode
  N7: Parte1.D2, U1.DB7
  N8: Parte1.D3_PWM, U1.DB6
  N9: Parte1.D4, U1.DB5
  N10: Parte1.D5_PWM, U1.DB4
  N11: Parte1.D6_PWM, R3.Pin_1
  5V: Parte1.5V, R1.pin_0, T1.+Vs, U1.VDD, U1.A, M1.pin_1, R5.Pin_0
  N12: U1.VO, S1.Pin_1, S1.Pin_2
  N13: LED1.anode, R3.Pin_0
  N14: LED2.anode, R4.Pin_0
  N15: M1.pin_2, D1.cathode
  N16: S1.Pin_3, S1.Pin_4, R5.Pin_1
